// Logisim project D-FLIP FLOP.circ as structural Verilog: 1 circuit, main circuit main
module main (
  input  D,
  output Q,
  output Q_BAR
);

  wire CLOCK_out, nand_1_out, nand_2_out, not_1_out;

  Clock CLOCK (.out(CLOCK_out));
  not not_1 (not_1_out, D);
  nand nand_1 (nand_1_out, D, CLOCK_out);
  nand nand_2 (nand_2_out, not_1_out, CLOCK_out);
  nand nand_3 (Q, nand_1_out, Q_BAR);
  nand nand_4 (Q_BAR, Q, nand_2_out);

  // Notes on the sheet:
  //   D-FLIP FLOP
endmodule
