// Logisim project SR LATCH.circ as structural Verilog: 1 circuit, main circuit main
// S
module main (
  input  S_prime,
  input  R_prime,
  output Q,
  output Q_prime
);

  nand nand_1 (Q, S_prime, Q_prime);
  nand nand_2 (Q_prime, Q, R_prime);

  // Notes on the sheet:
  //   SR LATCH
endmodule
