// Logisim project T-FLIP FLOP.circ as structural Verilog: 1 circuit, main circuit main
module main (
  input  T,
  output Q,
  output Q_prime
);

  wire CLOCK_out, nand_1_out, nand_2_out;

  Clock CLOCK (.out(CLOCK_out));
  nand nand_1 (nand_1_out, Q_prime, T, CLOCK_out);
  nand nand_2 (nand_2_out, CLOCK_out, T, Q);
  nand nand_3 (Q, nand_1_out, Q_prime);
  nand nand_4 (Q_prime, Q, nand_2_out);

  // Notes on the sheet:
  //   T FLIP FLOP
endmodule
